# Fritzing sketch project one (saved by Fritzing 0.9.9b)
breadboards: 2

parts:
  LCD1 = LCD screen
  PSU1 = Adjustable Breadboard Power Supply
  R1 = Trimmer Potentiometer [maximum_resistance=10kΩ package=THT]
  Part1 = RFID-RC522-v2
  A1 = Raspberry Pi 5
  DS1 = DS18B20 1-Wire Temperature Sensor [part_number=DS18B20]
  R2 = Resistor [tolerance=±5% resistance=10k package=THT]
  R3 = Resistor [tolerance=±5% resistance=10k package=THT]
  M1 = Dagu DGServo 9g (Top view) [part_number=RS001B]
  U1 = PCF8574 [package="DIP16 [THT]"]
  R4 = Photocell (LDR) [package=THT]
  R5 = Resistor [tolerance=±5% resistance=220 package=THT]
  ADC1 = MCP3008 [package=dil16]

nets (from the schematic view):
  N1: LCD1.VSS, LCD1.LED-, PSU1.Vin-, R1.leg2
  N2: LCD1.VDD, PSU1.Vin+, R1.leg1
  N3: LCD1.V0, LCD1.LED+, R1.wiper
  N4: LCD1.RS, A1.GPIO20
  N5: LCD1.E, A1.GPIO21
  N6: LCD1.DB0, U1.P0
  N7: LCD1.DB1, U1.P1
  N8: LCD1.DB2, U1.P2
  N9: LCD1.DB3, U1.P3
  N10: LCD1.DB4, U1.P4
  N11: LCD1.DB5, U1.P5
  N12: LCD1.DB6, U1.P6
  N13: LCD1.DB7, U1.P7
  N14: PSU1.Vout+, Part1.3.3V, R5.Pin_0
  GND: PSU1.Vout-, Part1.RST, A1.GND, DS1.GND, M1.gnd, U1.A0, U1.A1, U1.A2, U1.GND, R4.pin_1, ADC1.DGND, ADC1.AGND
  N15: Part1.SDA, A1.GPIO8
  N16: Part1.SCK, A1.GPIO11, ADC1.CLK
  N17: Part1.MOSI, A1.GPIO10, ADC1.Dout
  N18: Part1.MISO, A1.GPIO9, ADC1.Din
  N19: Part1.IRQ, A1.GPIO26
  N20: Part1.GND, A1.GPIO22
  N21: A1.GPIO2, U1.SDA
  N22: A1.GPIO3, U1.SCL
  N23: A1.GPIO4, DS1.DQ, R2.Pin_0, R3.Pin_0
  N24: A1.GPIO24, M1.pulse
  N25: A1.GPIO7, ADC1.CS/SHDN
  N26: DS1.VDD, R2.Pin_1, R3.Pin_1
  VCC: M1.vcc, U1.VCC
  N27: R4.pin_0, R5.Pin_1, ADC1.CH0
  N28: ADC1.VREF, ADC1.VDD

custom parts:
  RFID-RC522-v2: A simple China made RFID-RC522 Reader; do check the pin labels, as this is a MFRC522 based clone.
  Raspberry Pi 5: The RPi5, a faster version of the awesome Raspberry Pi4B ARM Board with 40 pin gpio.
